// Logisim project COA_CPU_miniproject.circ as structural Verilog: 3 circuits, main circuit main
module main (
  output [3:0] out_1,
  output [7:0] dbus,
  output [7:0] r1,
  output [7:0] r2,
  output [1:0] dregsel,
  output [7:0] r3,
  output [7:0] dval,
  output out_8,
  output [7:0] r4,
  output [7:0] sourceval,
  output [1:0] sregsel
);

  wire addresssel, and_1_out, and_4_out, and_5_out, and_7_out, clock_1_out, clock_2_out, clock_3_out,
       demultiplexer_1_out0, demultiplexer_1_out1, demultiplexer_1_out2, demultiplexer_1_out3, dwrite, halt,
       multiplexer_3_out, muxsel, not_1_out, not_2_out, not_3_out, not_4_out, not_5_out, not_6_out, or_1_out,
       or_2_out, pcsel, phase1, phase2, phase3;
  wire [1:0] alusel, multiplexer_7_out, phase;
  wire [7:0] adder_1_out, alu_1_output, MA_q, multiplexer_1_out, multiplexer_2_out, PC_q, ram_1_data;

  Demultiplexer #(.select(2), .enable("false")) demultiplexer_1 (
    .out0(demultiplexer_1_out0), .out1(demultiplexer_1_out1), .out2(demultiplexer_1_out2),
    .out3(demultiplexer_1_out3), .in(dwrite), .sel(dregsel));
  Multiplexer #(.width(8), .enable("false")) multiplexer_1 (
    .in0(MA_q), .in1(adder_1_out), .out(multiplexer_1_out), .sel(pcsel));
  and and_1 (and_1_out, out_1[3], phase2);
  Clock clock_1 (.out(clock_1_out));
  Register PC (.D(multiplexer_1_out), .en(out_8), .Q(PC_q), .clk(clock_1_out));  // open: clr
  Register MA (.D(ram_1_data), .en(and_1_out), .Q(MA_q), .clk(clock_1_out));  // open: clr
  Adder adder_1 (.a(8'h1), .b(PC_q), .out(adder_1_out));  // open: cin, cout
  Multiplexer #(.width(8), .enable("false")) multiplexer_2 (
    .in0(PC_q), .in1(MA_q), .out(multiplexer_2_out), .sel(muxsel));
  not not_1 (not_1_out, out_1[1]);
  not not_2 (not_2_out, out_1[2]);
  Multiplexer #(.select(4), .enable("false")) multiplexer_3 (
    .in0(1'b1), .in1(1'b1), .in2(1'b1), .in3(1'b1), .in4(1'b1), .in5(1'b1), .in6(1'b1), .in7(1'b1),
    .in9(1'b0), .in10(1'b1), .in12(1'b0), .out(multiplexer_3_out), .sel(out_1));  // open: in8, in11, in13, in14, in15
  Register register_1 (.D(dval), .en(demultiplexer_1_out0), .Q(r1), .clk(clock_2_out));  // open: clr
  Register register_2 (.D(dval), .en(demultiplexer_1_out1), .Q(r2), .clk(clock_2_out));  // open: clr
  Register register_3 (.D(dval), .en(demultiplexer_1_out2), .Q(r3), .clk(clock_2_out));  // open: clr
  Register register_4 (.D(dval), .en(demultiplexer_1_out3), .Q(r4), .clk(clock_2_out));  // open: clr
  Clock clock_2 (.out(clock_2_out));
  and and_2 (addresssel, out_1[0], not_1_out, phase3, not_2_out, out_1[3]);
  and and_3 (dwrite, multiplexer_3_out, phase3);
  RAM #(.bus("separate")) ram_1 (
    .addr(multiplexer_2_out), .din(dbus), .data(ram_1_data), .str(addresssel), .sel(halt), .clk(clock_1_out));  // open: ld, clr
  Multiplexer #(.select(2), .width(8), .enable("false")) multiplexer_4 (
    .in0(r1), .in1(r2), .in2(r3), .in3(r4), .out(dbus), .sel(dregsel));
  Multiplexer #(.select(2), .width(8), .enable("false")) multiplexer_5 (
    .in0(r1), .in1(r2), .in2(r3), .in3(r4), .out(sourceval), .sel(sregsel));
  Register IR (.D(ram_1_data), .en(phase1), .Q({out_1, dregsel, sregsel}), .clk(clock_1_out));  // open: clr
  Multiplexer #(.select(2), .width(8), .enable("false")) multiplexer_6 (
    .in1(sourceval), .in2(ram_1_data), .in3(alu_1_output), .out(dval), .sel(alusel));  // open: in0
  alu alu_1 (.dvalue(dbus), .sval(sourceval), .select(out_1[2:0]), .\output (alu_1_output));
  Multiplexer #(.select(4), .width(2), .enable("false")) multiplexer_7 (
    .in0(2'b11), .in1(2'b11), .in2(2'b11), .in3(2'b11), .in4(2'b11), .in5(2'b11), .in6(2'b00), .in7(2'b01),
    .in9(2'b00), .in10(2'b10), .in12(2'b00), .out(multiplexer_7_out), .sel(out_1));  // open: in8, in11, in13, in14, in15
  Counter #(.width(2), .max('h3)) counter_1 (
    .Q(phase), .clk(clock_3_out), .clr(and_4_out));  // open: load, D, count, carry
  Clock clock_3 (.out(clock_3_out));
  Decoder #(.select(2), .enable("false")) decoder_1 (
    .out0(phase1), .out1(phase2), .out2(phase3), .sel(phase));  // open: out3
  or or_1 (or_1_out, out_1[0], out_1[1]);
  not not_3 (not_3_out, out_1[2]);
  and and_4 (and_4_out, phase[1], phase[0]);
  not not_4 (not_4_out, phase3);
  not not_5 (not_5_out, out_1[3]);
  not not_6 (not_6_out, out_1[0]);
  and and_5 (and_5_out, out_1[3], out_1[2]);
  Multiplexer #(.select(2), .width(2), .enable("false")) multiplexer_8 (
    .in0(2'b00), .in1(2'b00), .in2(multiplexer_7_out), .in3(2'b00), .out(alusel), .sel(phase));
  or or_2 (or_2_out, phase1, phase2);
  and and_6 (pcsel, or_2_out, not_4_out);
  and and_7 (and_7_out, not_5_out, out_1[2], out_1[1], not_6_out);
  Multiplexer #(.select(2), .enable("false")) multiplexer_9 (
    .in0(1'b1), .in1(out_1[3]), .in2(and_5_out), .out(out_8), .sel(phase));  // open: in3
  and and_8 (muxsel, or_1_out, phase3, not_3_out, out_1[3]);
  not not_7 (halt, and_7_out);

  // Other names for the same wires on the sheet: bit7 = out_1[3]; op1op2[3:0] = out_1; pcload = out_8;
  //   bit4 = out_1[0]; select[2:0] = out_1[2:0]; bit5 = out_1[1]; bit6 = out_1[2]
endmodule

module \reg  (
  input  [1:0] in_1,
  input  [1:0] in_2,
  input  [2:0] in_3
);

  wire clock_1_out, demultiplexer_1_out0, demultiplexer_1_out1, demultiplexer_1_out2, demultiplexer_1_out3,
       demultiplexer_2_out0, demultiplexer_2_out1, demultiplexer_2_out2, demultiplexer_2_out3;
  wire [7:0] alu_1_output, controlled_buffer_1_out, controlled_buffer_2_out, controlled_buffer_3_out,
       controlled_buffer_4_out, controlled_buffer_7_out, controlled_buffer_10_out, register_1_q,
       register_2_q, register_3_q, register_4_q;

  Clock clock_1 (.out(clock_1_out));
  assign controlled_buffer_1_out = demultiplexer_1_out0 ? alu_1_output : 8'bz;  // Controlled_Buffer controlled_buffer_1
  Register register_1 (.D(controlled_buffer_1_out), .Q(register_1_q), .clk(clock_1_out));  // open: en, clr
  assign controlled_buffer_2_out = demultiplexer_2_out0 ? register_1_q : 8'bz;  // Controlled_Buffer controlled_buffer_2
  assign controlled_buffer_3_out = demultiplexer_1_out0 ? register_1_q : 8'bz;  // Controlled_Buffer controlled_buffer_3
  Demultiplexer #(.select(2)) demultiplexer_1 (
    .out0(demultiplexer_1_out0), .out1(demultiplexer_1_out1), .out2(demultiplexer_1_out2),
    .out3(demultiplexer_1_out3), .in(1'b1), .sel(in_1));  // open: en
  assign controlled_buffer_4_out = demultiplexer_1_out1 ? alu_1_output : 8'bz;  // Controlled_Buffer controlled_buffer_4
  Demultiplexer #(.select(2)) demultiplexer_2 (
    .out0(demultiplexer_2_out0), .out1(demultiplexer_2_out1), .out2(demultiplexer_2_out2),
    .out3(demultiplexer_2_out3), .in(1'b1), .sel(in_2));  // open: en
  Register register_2 (.D(controlled_buffer_4_out), .Q(register_2_q), .clk(clock_1_out));  // open: en, clr
  assign controlled_buffer_3_out = demultiplexer_1_out1 ? register_2_q : 8'bz;  // Controlled_Buffer controlled_buffer_5
  assign controlled_buffer_2_out = demultiplexer_2_out1 ? register_2_q : 8'bz;  // Controlled_Buffer controlled_buffer_6
  assign controlled_buffer_7_out = demultiplexer_1_out2 ? alu_1_output : 8'bz;  // Controlled_Buffer controlled_buffer_7
  Register register_3 (.D(controlled_buffer_7_out), .Q(register_3_q), .clk(clock_1_out));  // open: en, clr
  assign controlled_buffer_2_out = demultiplexer_2_out2 ? register_3_q : 8'bz;  // Controlled_Buffer controlled_buffer_8
  assign controlled_buffer_3_out = demultiplexer_1_out2 ? register_3_q : 8'bz;  // Controlled_Buffer controlled_buffer_9
  assign controlled_buffer_10_out = demultiplexer_1_out3 ? alu_1_output : 8'bz;  // Controlled_Buffer controlled_buffer_10
  Register register_4 (.D(controlled_buffer_10_out), .Q(register_4_q), .clk(clock_1_out));  // open: en, clr
  assign controlled_buffer_2_out = demultiplexer_2_out3 ? register_4_q : 8'bz;  // Controlled_Buffer controlled_buffer_11
  assign controlled_buffer_3_out = demultiplexer_1_out3 ? register_4_q : 8'bz;  // Controlled_Buffer controlled_buffer_12
  alu alu_1 (.dvalue(controlled_buffer_2_out), .sval(controlled_buffer_3_out), .select(in_3), .\output (alu_1_output));
endmodule

module alu (
  input  [7:0] dvalue,
  input  [7:0] sval,
  input  [2:0] select,
  output [7:0] \output 
);

  wire [7:0] adder_1_out, and_1_out, demultiplexer_1_out0, demultiplexer_1_out1, demultiplexer_1_out2,
       demultiplexer_1_out3, demultiplexer_1_out4, demultiplexer_1_out5, demultiplexer_2_out0,
       demultiplexer_2_out1, demultiplexer_2_out2, demultiplexer_2_out3, demultiplexer_2_out4,
       demultiplexer_2_out5, multiplier_1_out, or_1_out, subtractor_1_out, xor_1_out;

  Demultiplexer #(.select(3), .width(8), .enable("false")) demultiplexer_1 (
    .out0(demultiplexer_1_out0), .out1(demultiplexer_1_out1), .out2(demultiplexer_1_out2),
    .out3(demultiplexer_1_out3), .out4(demultiplexer_1_out4), .out5(demultiplexer_1_out5), .in(dvalue),
    .sel(select));  // open: out6, out7
  Demultiplexer #(.select(3), .width(8), .enable("false")) demultiplexer_2 (
    .out0(demultiplexer_2_out0), .out1(demultiplexer_2_out1), .out2(demultiplexer_2_out2),
    .out3(demultiplexer_2_out3), .out4(demultiplexer_2_out4), .out5(demultiplexer_2_out5), .in(sval),
    .sel(select));  // open: out6, out7
  Adder adder_1 (.a(demultiplexer_1_out0), .b(demultiplexer_2_out0), .out(adder_1_out));  // open: cin, cout
  Subtractor subtractor_1 (
    .a(demultiplexer_1_out1), .b(demultiplexer_2_out1), .out(subtractor_1_out));  // open: bin, bout
  Multiplier multiplier_1 (
    .a(demultiplexer_1_out2), .b(demultiplexer_2_out2), .out(multiplier_1_out));  // open: cin, cout
  assign and_1_out = demultiplexer_1_out3 & demultiplexer_2_out3;  // AND_Gate and_1, 8 bits wide
  assign or_1_out = demultiplexer_1_out4 | demultiplexer_2_out4;  // OR_Gate or_1, 8 bits wide
  assign xor_1_out = demultiplexer_1_out5 ^ demultiplexer_2_out5;  // XOR_Gate xor_1, 8 bits wide
  Multiplexer #(.select(3), .width(8), .disabled(0), .enable("false")) multiplexer_1 (
    .in0(adder_1_out), .in1(subtractor_1_out), .in2(multiplier_1_out), .in3(and_1_out), .in4(or_1_out),
    .in5(xor_1_out), .out(\output ), .sel(select));  // open: in6, in7
endmodule
